// Logisim project Calculadora Binária.circ as structural Verilog: 6 circuits, main circuit MeioSomador
module MeioSomador (
  input  A,
  input  B,
  output S,
  output Co
);

  and and_1 (Co, A, B);
  xor xor_1 (S, A, B);
endmodule

module Somador (
  input  A,
  input  B,
  input  CI,
  output s,
  output CO
);

  wire meiosomador_1_co, meiosomador_1_s, meiosomador_2_co;

  MeioSomador meiosomador_1 (.A(A), .B(B), .S(meiosomador_1_s), .Co(meiosomador_1_co));
  MeioSomador meiosomador_2 (.A(CI), .B(meiosomador_1_s), .S(s), .Co(meiosomador_2_co));
  or or_1 (CO, meiosomador_1_co, meiosomador_2_co);
endmodule

module Somador2Bits (
  input  A0,
  input  B0,
  input  A1,
  input  B1,
  output S0,
  output S1,
  output Co
);

  wire somador_1_co;

  Somador somador_1 (.A(A0), .B(B0), .CI(1'b0), .s(S0), .CO(somador_1_co));
  Somador somador_2 (.A(A1), .B(B1), .CI(somador_1_co), .s(S1), .CO(Co));
endmodule

module MeioSubtrator (
  input  A,
  input  B,
  output D,
  output Bo
);

  wire not_1_out;

  not not_1 (not_1_out, A);
  xor xor_1 (D, A, B);
  and and_1 (Bo, not_1_out, B);
endmodule

module Subtrator (
  input  A,
  input  B,
  input  BO_i,
  output DI_o,
  output BO_o
);

  wire meiosubtrator_1_bo, meiosubtrator_1_d, meiosubtrator_2_bo;

  MeioSubtrator meiosubtrator_1 (.A(A), .B(B), .D(meiosubtrator_1_d), .Bo(meiosubtrator_1_bo));
  MeioSubtrator meiosubtrator_2 (.A(meiosubtrator_1_d), .B(BO_i), .D(DI_o), .Bo(meiosubtrator_2_bo));
  or or_1 (BO_o, meiosubtrator_1_bo, meiosubtrator_2_bo);
endmodule

module Subtrator2Bits (
  input  A0,
  input  B0,
  input  A1,
  input  B1,
  output S,
  output S0,
  output Bo
);

  wire subtrator_1_bo_o;

  Subtrator subtrator_1 (.A(A0), .B(B0), .BO_i(1'b0), .DI_o(S0), .BO_o(subtrator_1_bo_o));
  Subtrator subtrator_2 (.A(A1), .B(B1), .BO_i(subtrator_1_bo_o), .DI_o(S), .BO_o(Bo));
endmodule
